// Digital circuit 4-bit-adder-carry.dig as structural Verilog
module _4_bit_adder_carry (
  input  [3:0] A,
  input  [3:0] B,
  input  Carry_In,
  output Overflow_Bit___Flag,
  output [3:0] Output
);

  wire _1_bit_adder_1_p3, _1_bit_adder_2_p3, _1_bit_adder_3_p3;

  // _1_bit_adder _1_bit_adder_1: pin names not known; wires that end beside it: A[3], B[3], _1_bit_adder_1_p3, Output[3], Overflow_Bit___Flag
  // _1_bit_adder _1_bit_adder_2: pin names not known; wires that end beside it: A[2], B[2], _1_bit_adder_2_p3, Output[2], _1_bit_adder_1_p3
  // _1_bit_adder _1_bit_adder_3: pin names not known; wires that end beside it: A[1], B[1], _1_bit_adder_3_p3, Output[1], _1_bit_adder_2_p3
  // _1_bit_adder _1_bit_adder_4: pin names not known; wires that end beside it: A[0], B[0], Carry_In, Output[0], _1_bit_adder_3_p3
endmodule
