// Digital circuit 4-bit-register.dig as structural Verilog
module _4_bit_register (
  input  [3:0] Input,
  input  Clock,
  output [3:0] Store
);

  D_FF d_ff_1 (.D(Input[3]), .C(Clock), .Q(Store[3]));  // open: nQ
  D_FF d_ff_2 (.D(Input[2]), .C(Clock), .Q(Store[2]));  // open: nQ
  D_FF d_ff_3 (.D(Input[1]), .C(Clock), .Q(Store[1]));  // open: nQ
  D_FF d_ff_4 (.D(Input[0]), .C(Clock), .Q(Store[0]));  // open: nQ
endmodule
