// Digital circuit 4bitProcessor.dig as structural Verilog
module _4bitProcessor (
  input  clk,
  input  CTRL_IR,
  input  [1:0] CTRL_PC,
  input  [3:0] Manual_Addr,
  input  CTRL_Mem,
  input  [3:0] instr_mem_input
);

  wire [3:0] arithmetic_unit_1_d, register_file_1_read_data_1, register_file_1_read_data_2;
  wire [7:0] opcode3_write_selector_1_write_ctrl;
  wire [15:0] instr_mem_module_4_bit_1_ir_output;

  instr_mem_module_4_bit instr_mem_module_4_bit_1 (
    .clk(clk), .CTRL_IR(CTRL_IR), .CTRL_PC(CTRL_PC), .Manual_Address_Override(Manual_Addr),
    .CTRL_MEM(CTRL_Mem), .instr_mem_input(instr_mem_input), .IR_output(instr_mem_module_4_bit_1_ir_output));
  OpCode3_write_selector opcode3_write_selector_1 (
    .OpCode3(instr_mem_module_4_bit_1_ir_output[1:0]), .write_ctrl(opcode3_write_selector_1_write_ctrl));
  Register_File register_file_1 (
    .Select_read_1(instr_mem_module_4_bit_1_ir_output[5:4]),
    .Select_read_2(instr_mem_module_4_bit_1_ir_output[3:2]), .clk(clk), .Write_data(arithmetic_unit_1_d),
    .Select_write(instr_mem_module_4_bit_1_ir_output[1:0]),
    .ctrl_registers(opcode3_write_selector_1_write_ctrl), .Read_data_1(register_file_1_read_data_1),
    .Read_data_2(register_file_1_read_data_2));
  Arithmetic_Unit arithmetic_unit_1 (
    .A(register_file_1_read_data_1), .B(register_file_1_read_data_2),
    .S_1_S_0_C_in(instr_mem_module_4_bit_1_ir_output[8:6]), .D(arithmetic_unit_1_d));  // open: overflow
endmodule
