// Digital circuit Arithmetic_Unit.dig as structural Verilog
module Arithmetic_Unit (
  input  [3:0] A,
  input  [3:0] B,
  input  [2:0] S_1_S_0_C_in,
  output [3:0] D,
  output overflow
);

  wire [3:0] multiplexer_1_out, not_1_out, not_2_out;

  assign not_1_out = ~B;  // Not not_1, 4 bits wide
  assign not_2_out = ~4'b0000;  // Not not_2, 4 bits wide
  Multiplexer #(.Bits(4), .Selector_Bits(2)) multiplexer_1 (
    .sel(S_1_S_0_C_in[2:1]), .in_0(B), .in_1(not_1_out), .in_2(4'b0000), .in_3(not_2_out),
    .out(multiplexer_1_out));
  _4_bit_adder_carry _4_bit_adder_carry_1 (
    .A(A), .B(multiplexer_1_out), .Carry_In(S_1_S_0_C_in[0]), .Overflow_Bit___Flag(overflow), .Output(D));

  // Notes on the sheet:
  //   S_1_S_0_C_in: Add
  //   Add with Carry
  //   Subtract with Borrow
  //   Subtract
  //   Transfer A
  //   Increment A
  //   Decrement A
  //   Transfer A
endmodule
