// Digital circuit IR.dig as structural Verilog
module IR (
  input  CTRL__Load___Read,
  input  clk,
  input  [3:0] Input,
  output [3:0] Output
);

  wire [3:0] multiplexer_1_out;

  Multiplexer #(.Bits(4)) multiplexer_1 (.sel(CTRL__Load___Read), .in_0(Input), .in_1(Output), .out(multiplexer_1_out));
  _4_bit_register _4_bit_register_1 (.Input(multiplexer_1_out), .Clock(clk), .Store(Output));
endmodule
