// Digital circuit Register_File.dig as structural Verilog
module Register_File (
  input  [1:0] Select_read_1,
  input  [1:0] Select_read_2,
  input  clk,
  input  [3:0] Write_data,
  input  [1:0] Select_write,
  input  [7:0] ctrl_registers,
  output [3:0] Read_data_1,
  output [3:0] Read_data_2
);

  wire [3:0] demultiplexer_1_out_0, demultiplexer_1_out_1, demultiplexer_1_out_2, demultiplexer_1_out_3,
       R_0_store, R_1_store, R_2_store, R_3_store;

  Demultiplexer #(.Bits(4), .Selector_Bits(2)) demultiplexer_1 (
    .sel(Select_write), .in(Write_data), .out_0(demultiplexer_1_out_0), .out_1(demultiplexer_1_out_1),
    .out_2(demultiplexer_1_out_2), .out_3(demultiplexer_1_out_3));
  _4_bit_register_ctrl R_0 (
    .Input(demultiplexer_1_out_0), .Clock(clk), .CTRL__Read___Write___Clear(ctrl_registers[1:0]),
    .Store(R_0_store));
  _4_bit_register_ctrl R_1 (
    .Input(demultiplexer_1_out_1), .Clock(clk), .CTRL__Read___Write___Clear(ctrl_registers[3:2]),
    .Store(R_1_store));
  _4_bit_register_ctrl R_2 (
    .Input(demultiplexer_1_out_2), .Clock(clk), .CTRL__Read___Write___Clear(ctrl_registers[5:4]),
    .Store(R_2_store));
  _4_bit_register_ctrl R_3 (
    .Input(demultiplexer_1_out_3), .Clock(clk), .CTRL__Read___Write___Clear(ctrl_registers[7:6]),
    .Store(R_3_store));
  Multiplexer #(.Bits(4), .Selector_Bits(2)) multiplexer_1 (
    .sel(Select_read_1), .in_0(R_0_store), .in_1(R_1_store), .in_2(R_2_store), .in_3(R_3_store),
    .out(Read_data_1));
  Multiplexer #(.Selector_Bits(2), .Bits(4)) multiplexer_2 (
    .sel(Select_read_2), .in_0(R_0_store), .in_1(R_1_store), .in_2(R_2_store), .in_3(R_3_store),
    .out(Read_data_2));
endmodule
