// Digital circuit Registers_DRAM.dig as structural Verilog
module Registers_DRAM (
  input  [3:0] Data,
  input  Read___Write,
  input  clk,
  input  [3:0] Address,
  output [3:0] Output
);

  wire delay_1_out, demultiplexer_1_out_0, demultiplexer_1_out_1, demultiplexer_1_out_2,
       demultiplexer_1_out_3, demultiplexer_1_out_4, demultiplexer_1_out_5, demultiplexer_1_out_6,
       demultiplexer_1_out_7, demultiplexer_1_out_8, demultiplexer_1_out_9, demultiplexer_1_out_10,
       demultiplexer_1_out_11, demultiplexer_1_out_12, demultiplexer_1_out_13, demultiplexer_1_out_14,
       demultiplexer_1_out_15;
  wire [3:0] multiplexer_1_out, R_0_store, R_1_store, R_2_store, R_3_store, R_4_store, R_5_store, R_6_store,
       R_7_store, R_8_store, R_9_store, R_10_store, R_11_store, R_12_store, R_13_store, R_14_store,
       R_15_store;

  Delay #(.delayTime(5)) delay_1 (.in(clk), .out(delay_1_out));
  Demultiplexer #(.Selector_Bits(4)) demultiplexer_1 (
    .sel(Address), .in(delay_1_out), .out_0(demultiplexer_1_out_0), .out_1(demultiplexer_1_out_1),
    .out_2(demultiplexer_1_out_2), .out_3(demultiplexer_1_out_3), .out_4(demultiplexer_1_out_4),
    .out_5(demultiplexer_1_out_5), .out_6(demultiplexer_1_out_6), .out_7(demultiplexer_1_out_7),
    .out_8(demultiplexer_1_out_8), .out_9(demultiplexer_1_out_9), .out_10(demultiplexer_1_out_10),
    .out_11(demultiplexer_1_out_11), .out_12(demultiplexer_1_out_12), .out_13(demultiplexer_1_out_13),
    .out_14(demultiplexer_1_out_14), .out_15(demultiplexer_1_out_15));
  Multiplexer #(.Bits(4)) multiplexer_1 (.sel(Read___Write), .in_0(Output), .in_1(Data), .out(multiplexer_1_out));
  _4_bit_register R_15 (.Input(multiplexer_1_out), .Clock(demultiplexer_1_out_15), .Store(R_15_store));
  _4_bit_register R_14 (.Input(multiplexer_1_out), .Clock(demultiplexer_1_out_14), .Store(R_14_store));
  _4_bit_register R_13 (.Input(multiplexer_1_out), .Clock(demultiplexer_1_out_13), .Store(R_13_store));
  _4_bit_register R_12 (.Input(multiplexer_1_out), .Clock(demultiplexer_1_out_12), .Store(R_12_store));
  _4_bit_register R_11 (.Input(multiplexer_1_out), .Clock(demultiplexer_1_out_11), .Store(R_11_store));
  _4_bit_register R_10 (.Input(multiplexer_1_out), .Clock(demultiplexer_1_out_10), .Store(R_10_store));
  _4_bit_register R_9 (.Input(multiplexer_1_out), .Clock(demultiplexer_1_out_9), .Store(R_9_store));
  _4_bit_register R_8 (.Input(multiplexer_1_out), .Clock(demultiplexer_1_out_8), .Store(R_8_store));
  _4_bit_register R_7 (.Input(multiplexer_1_out), .Clock(demultiplexer_1_out_7), .Store(R_7_store));
  _4_bit_register R_6 (.Input(multiplexer_1_out), .Clock(demultiplexer_1_out_6), .Store(R_6_store));
  _4_bit_register R_5 (.Input(multiplexer_1_out), .Clock(demultiplexer_1_out_5), .Store(R_5_store));
  _4_bit_register R_4 (.Input(multiplexer_1_out), .Clock(demultiplexer_1_out_4), .Store(R_4_store));
  _4_bit_register R_3 (.Input(multiplexer_1_out), .Clock(demultiplexer_1_out_3), .Store(R_3_store));
  _4_bit_register R_2 (.Input(multiplexer_1_out), .Clock(demultiplexer_1_out_2), .Store(R_2_store));
  _4_bit_register R_1 (.Input(multiplexer_1_out), .Clock(demultiplexer_1_out_1), .Store(R_1_store));
  _4_bit_register R_0 (.Input(multiplexer_1_out), .Clock(demultiplexer_1_out_0), .Store(R_0_store));
  Multiplexer #(.Selector_Bits(4), .Bits(4)) multiplexer_2 (
    .sel(Address), .in_0(R_0_store), .in_1(R_1_store), .in_2(R_2_store), .in_3(R_3_store), .in_4(R_4_store),
    .in_5(R_5_store), .in_6(R_6_store), .in_7(R_7_store), .in_8(R_8_store), .in_9(R_9_store),
    .in_10(R_10_store), .in_11(R_11_store), .in_12(R_12_store), .in_13(R_13_store), .in_14(R_14_store),
    .in_15(R_15_store), .out(Output));
endmodule
