// Digital circuit instr-mem-module-4-bit.dig as structural Verilog
module instr_mem_module_4_bit (
  input  clk,
  input  CTRL_IR,
  input  [1:0] CTRL_PC,
  input  [3:0] Manual_Address_Override,
  input  CTRL_MEM,
  input  [3:0] instr_mem_input,
  output [15:0] IR_output
);

  wire and_1_out, delay_1_out, demultiplexer_1_out_0, demultiplexer_1_out_1, demultiplexer_1_out_2,
       demultiplexer_1_out_3;
  wire [3:0] demultiplexer_2_out_0, demultiplexer_2_out_1, demultiplexer_2_out_2, demultiplexer_2_out_3,
       IR_0_output, IR_1_output, IR_2_output, IR_3_output, memory_output, PC_address_output;

  PC PC (
    .CTRL__Inc___Write___Reset(CTRL_PC), .Manual_Load(Manual_Address_Override), .clk(clk),
    .Address_Output(PC_address_output));
  Registers_DRAM memory (
    .Data(instr_mem_input), .Read___Write(CTRL_MEM), .clk(clk), .Address(PC_address_output),
    .Output(memory_output));
  Demultiplexer #(.Selector_Bits(2), .Default(1)) demultiplexer_1 (
    .sel(PC_address_output[1:0]), .in(CTRL_IR), .out_0(demultiplexer_1_out_0), .out_1(demultiplexer_1_out_1),
    .out_2(demultiplexer_1_out_2), .out_3(demultiplexer_1_out_3));
  Demultiplexer #(.Selector_Bits(2), .Bits(4)) demultiplexer_2 (
    .sel(PC_address_output[1:0]), .in(memory_output), .out_0(demultiplexer_2_out_0),
    .out_1(demultiplexer_2_out_1), .out_2(demultiplexer_2_out_2), .out_3(demultiplexer_2_out_3));
  IR IR_0 (.CTRL__Load___Read(demultiplexer_1_out_0), .clk(clk), .Input(demultiplexer_2_out_0), .Output(IR_0_output));
  IR IR_1 (.CTRL__Load___Read(demultiplexer_1_out_1), .clk(clk), .Input(demultiplexer_2_out_1), .Output(IR_1_output));
  IR IR_2 (.CTRL__Load___Read(demultiplexer_1_out_2), .clk(clk), .Input(demultiplexer_2_out_2), .Output(IR_2_output));
  IR IR_3 (.CTRL__Load___Read(demultiplexer_1_out_3), .clk(clk), .Input(demultiplexer_2_out_3), .Output(IR_3_output));
  and and_1 (and_1_out, ~PC_address_output[0], ~PC_address_output[1]);  // And
  Delay #(.delayTime(5)) delay_1 (.in(and_1_out), .out(delay_1_out));
  assign IR_output = delay_1_out ? {IR_3_output, IR_2_output, IR_1_output, IR_0_output} : 16'bz;  // Driver driver_1
endmodule
